# Fritzing sketch STEM-FINITY-ESP-SERVO-POT-OLED-LED (saved by Fritzing 0.9.3b)
breadboards: 1

parts:
  U1 = NodeMCU V3.0
  OLED_I2C1 = OLED 128x64 I2C Monochrome Display
  U2 = POT [package=pot_alpha_rv16af-20]
  J1 = Basic Servo
  LED2 = smd LED [color="Red (633nm)" package="1206 [SMD]"]
  LED3 = smd LED [color="Red (633nm)" package="1206 [SMD]"]
  LED4 = smd LED [color="Yellow (595nm)" package="1206 [SMD]"]
  LED5 = smd LED [color="Yellow (595nm)" package="1206 [SMD]"]
  LED6 = smd LED [color="Green (555nm)" package="1206 [SMD]"]
  LED7 = smd LED [color="Green (555nm)" package="1206 [SMD]"]

nets:
  N1: U1.D0, J1.pulse
  N2: U1.D1, OLED_I2C1.SCK
  N3: U1.D2, OLED_I2C1.SDA
  N4: U1.D3, LED7.anode
  N5: U1.D4, LED6.anode
  3V3: U1.3V3, OLED_I2C1.VDD, U2.A, J1.vcc
  GND: U1.GND#6, U1.GND#13, U1.GND#16, U1.GND#33, OLED_I2C1.GND, U2.E, J1.gnd, LED2.cathode, LED3.cathode, LED4.cathode, LED5.cathode, LED6.cathode, LED7.cathode
  N6: U1.D5, LED5.anode
  N7: U1.D6, LED4.anode
  N8: U1.D7, LED2.anode
  N9: U1.D8, LED3.anode
  N10: U1.A0, U2.S

custom parts:
  NodeMCU V3.0: ESP8266 based NodeMCU
