# Fritzing sketch STEM-FINITY-ESP-SERVO-POT-OLED (saved by Fritzing 0.9.3b)
breadboards: 1

parts:
  U1 = NodeMCU V3.0
  OLED_I2C1 = OLED 128x64 I2C Monochrome Display
  U2 = POT [package=pot_alpha_rv16af-20]
  J1 = Basic Servo

nets:
  N1: U1.D0, J1.pulse
  N2: U1.D1, OLED_I2C1.SCK
  N3: U1.D2, OLED_I2C1.SDA
  3V3: U1.3V3, OLED_I2C1.VDD, U2.A, J1.vcc
  GND: U1.GND#6, U1.GND#13, U1.GND#16, U1.GND#33, OLED_I2C1.GND, U2.E, J1.gnd
  N4: U1.A0, U2.S

custom parts:
  NodeMCU V3.0: ESP8266 based NodeMCU
